# Fritzing sketch wiring_dht20 (saved by Fritzing 0.9.10b)
breadboards: 1

parts:
  A4 = DHT22 module
  U1 = ESP32-38PinWide [part_number=ESP32-38PinWide]
  A6 = DHT22 module
  LED1 = smd LED [color="Red (633nm)" package="0805 [SMD]"]
  LED2 = smd LED [color="Yellow (585nm)" package="0805 [SMD]"]
  LED3 = smd LED [color="Green (565nm)" package="0805 [SMD]"]
  R1 = Resistor [tolerance=±5% resistance=220 package="0402 [SMD]"]
  R2 = Resistor [tolerance=±5% resistance=220 package="0402 [SMD]"]
  R3 = Resistor [tolerance=±5% resistance=220 package="0402 [SMD]"]

nets:
  N1: A4.+, A6.+
  N2: A4.SDA, U1.GPIO21
  N3: A4.-, A6.-, LED1.cathode, LED2.cathode, LED3.cathode
  N4: A4.SCL, U1.GPIO22
  N5: U1.GPIO16, R1.Pin_0
  N6: U1.GPIO5, A6.Out
  N7: U1.GPIO18, R3.Pin_0
  N8: U1.GPIO19, R2.Pin_0
  N9: LED1.anode, R3.Pin_1
  N10: LED2.anode, R2.Pin_1
  N11: LED3.anode, R1.Pin_1

custom parts:
  DHT22 module: DHT22 module. Pins VCC Data GND.
  ESP32-38PinWide: Generic 38-Pin ESP32 with wide format (only access to one side of pins on a breadboard) based on Stephen Lilley's HiLetgo ESP-WROOM-32 ESP32 ESP-32S Development Board.
  DHT22 module: DHT22 module. Pins VCC Data GND.
